# Fritzing sketch Fritzing (saved by Fritzing 0.9.3b)

parts:
  Part2 = Arduino Uno (Rev3) - ICSP
  Part3 = Monster Moto Shield
  Adafruit_HUZZAH_ESP8266_Breakout1 = Adafruit HUZZAH ESP8266 Breakout [part_number=2471]
  R2 = Resistor [tolerance=±5% resistance=10k package="2512 [SMD]"]
  R3 = Temperature Sensor (Thermistor) [thermistor_type=NTC package=THT]

nets:
  N1: Part2.A0, R2.Pin_0, R3.pin_0
  N2: Part2.D8, Part3.INB1_-_D8
  N3: Part2.D9_PWM, Part3.INB2_-_D9
  N4: Part2.D10_PWM/SS, Adafruit_HUZZAH_ESP8266_Breakout1.#15
  N5: Part2.D11_PWM/MOSI, Adafruit_HUZZAH_ESP8266_Breakout1.#12
  N6: Part2.D4, Part3.INA2_-_D4
  N7: Part2.D5_PWM, Part3.PWM1_-_D5
  N8: Part2.D6_PWM, Part3.PWM2_-_D6
  N9: Part2.D7, Part3.INA1_-_D7
  N10: Part2.5V, Adafruit_HUZZAH_ESP8266_Breakout1.V+, R3.pin_1
  GND: Part2.GND, Part3.GND, Part3.GND_-_GND@0, Adafruit_HUZZAH_ESP8266_Breakout1.GND, R2.Pin_1
